// Logisim project ROM.circ as structural Verilog: 1 circuit, main circuit main
module main (
  input  [6:0] in_1,
  input  in_2,
  input  in_3,
  input  in_4,
  output [6:0] out_5
);

  wire clock_1_out;

  ROM #(.addrWidth(7), .dataWidth(7)) rom_1 (.addr(in_1), .data(out_5), .sel(in_2));
  Clock clock_1 (.out(clock_1_out));
  TTY tty_1 (.data(out_5), .clk(clock_1_out), .we(in_3), .clr(in_4));

  // Notes on the sheet:
  //   contents of rom_1 (hex, n*v repeats v):
  //   41 49 59 64 4*41 41*0 41 41 19*0 41 32*0 41 23*0 41
endmodule
