// Logisim project demultiplexer.circ as structural Verilog: 1 circuit, main circuit main
module main (
  input  A,
  input  B,
  input  C,
  input  D,
  input  S0,
  input  S1,
  input  in_7,
  input  in_8,
  input  in_9,
  input  in_10,
  input  in_11,
  input  in_12,
  input  [1:0] in_13,
  input  in_14,
  input  in_15,
  input  [1:0] in_16,
  output out_17,
  output out_18,
  output out_19,
  output out_20,
  output out_21,
  output out_22,
  output out_23,
  output out_24,
  output out_25,
  output out_26,
  output out_27
);

  wire and_1_out, and_2_out, and_3_out, and_4_out, and_9_out, not_1_out, not_2_out, not_3_out, not_4_out;

  not not_1 (not_1_out, S0);
  not not_2 (not_2_out, S1);
  and and_1 (and_1_out, not_1_out, not_2_out);
  and and_2 (and_2_out, not_1_out, S1);
  and and_3 (and_3_out, S0, not_2_out);
  and and_4 (and_4_out, S0, S1);
  and and_5 (out_17, A, and_1_out);
  and and_6 (out_18, B, and_2_out);
  and and_7 (out_19, C, and_3_out);
  and and_8 (out_20, D, and_4_out);
  not not_3 (not_3_out, in_7);
  not not_4 (not_4_out, in_8);
  and and_9 (and_9_out, not_3_out, not_4_out);
  not not_5 (out_21, and_9_out);
  or or_1 (out_22, in_8, in_7);
  Multiplexer #(.select(2)) multiplexer_1 (
    .in0(in_9), .in1(in_10), .in2(in_11), .in3(in_12), .out(out_23), .sel(in_13), .en(in_14));
  Decoder #(.select(2)) decoder_1 (.out0(out_24), .out1(out_25), .out2(out_26), .out3(out_27), .sel(in_16), .en(in_15));
endmodule
