// Logisim project shift register.circ as structural Verilog: 1 circuit, main circuit main
module main (
  input  in_1,
  input  in_2,
  input  in_3,
  input  in_4,
  input  in_5,
  input  in_6,
  input  [1:0] in_7,
  output out_8,
  output out_9,
  output out_10,
  output out_11
);

  wire button_1_out, d_ff_1_qn, d_ff_2_qn, d_ff_3_qn, d_ff_4_qn, multiplexer_1_out, multiplexer_2_out,
       multiplexer_3_out, multiplexer_4_out;

  Multiplexer #(.select(2)) multiplexer_1 (
    .in0(in_1), .in1(out_9), .in2(in_6), .in3(d_ff_1_qn), .out(multiplexer_1_out), .sel(in_7), .en(1'b1));
  Button button_1 (.out(button_1_out));
  D_Flip_Flop d_ff_1 (.clk(button_1_out), .D(multiplexer_1_out), .Q(out_8), .Qn(d_ff_1_qn));  // open: preset, en, reset
  Multiplexer #(.select(2)) multiplexer_2 (
    .in0(in_2), .in1(out_10), .in2(out_8), .in3(d_ff_2_qn), .out(multiplexer_2_out), .sel(in_7), .en(1'b1));
  D_Flip_Flop d_ff_2 (.clk(button_1_out), .D(multiplexer_2_out), .Q(out_9), .Qn(d_ff_2_qn));  // open: preset, en, reset
  Multiplexer #(.select(2)) multiplexer_3 (
    .in0(in_3), .in1(out_11), .in2(out_9), .in3(d_ff_3_qn), .out(multiplexer_3_out), .sel(in_7), .en(1'b1));
  D_Flip_Flop d_ff_3 (
    .clk(button_1_out), .D(multiplexer_3_out), .Q(out_10), .Qn(d_ff_3_qn));  // open: preset, en, reset
  Multiplexer #(.select(2)) multiplexer_4 (
    .in0(in_4), .in1(in_5), .in2(out_10), .in3(d_ff_4_qn), .out(multiplexer_4_out), .sel(in_7), .en(1'b1));
  D_Flip_Flop d_ff_4 (
    .clk(button_1_out), .D(multiplexer_4_out), .Q(out_11), .Qn(d_ff_4_qn));  // open: preset, en, reset
endmodule
