// Logisim project shift register.circ as structural Verilog: 1 circuit, main circuit main
module main (
  input  in_1,
  input  in_2,
  input  in_3,
  input  in_4,
  input  RL,
  input  LR,
  input  [1:0] in_7,
  output out_8,
  output out_9,
  output out_10,
  output out_11
);

  wire button_1_out, multiplexer_1_out, multiplexer_2_out, multiplexer_3_out, multiplexer_4_out;

  Button button_1 (.out(button_1_out));
  D_Flip_Flop d_ff_1 (.clk(button_1_out), .D(multiplexer_1_out), .Q(out_8));  // open: Qn, preset, en, reset
  Multiplexer #(.select(2)) multiplexer_1 (
    .in0(in_1), .in1(out_9), .in2(LR), .in3(out_8), .out(multiplexer_1_out), .sel(in_7), .en(1'b1));
  Multiplexer #(.select(2)) multiplexer_2 (
    .in0(in_2), .in1(out_10), .in2(out_8), .in3(out_9), .out(multiplexer_2_out), .sel(in_7), .en(1'b1));
  D_Flip_Flop d_ff_2 (.clk(button_1_out), .D(multiplexer_2_out), .Q(out_9));  // open: Qn, preset, en, reset
  Multiplexer #(.select(2)) multiplexer_3 (
    .in0(in_3), .in1(out_11), .in2(out_9), .in3(out_10), .out(multiplexer_3_out), .sel(in_7), .en(1'b1));
  D_Flip_Flop d_ff_3 (.clk(button_1_out), .D(multiplexer_3_out), .Q(out_10));  // open: Qn, preset, en, reset
  Multiplexer #(.select(2)) multiplexer_4 (
    .in0(in_4), .in1(RL), .in2(out_10), .in3(out_11), .out(multiplexer_4_out), .sel(in_7), .en(1'b1));
  D_Flip_Flop d_ff_4 (.clk(button_1_out), .D(multiplexer_4_out), .Q(out_11));  // open: Qn, preset, en, reset
endmodule
