// Logisim project RAM.circ as structural Verilog: 1 circuit, main circuit main
module main (
  input  [7:0] Dados,
  input  Leitura_0__Escrita_1,
  input  [7:0] \Endereço ,
  input  in_4,
  input  in_5,
  input  Clock,
  output [7:0] out_7
);

  wire not_1_out;

  assign out_7 = Leitura_0__Escrita_1 ? Dados : 8'bz;  // Controlled_Buffer controlled_buffer_1
  not not_1 (not_1_out, Leitura_0__Escrita_1);
  RAM ram_1 (.addr(\Endereço ), .data(out_7), .sel(in_4), .clk(Clock), .ld(not_1_out), .clr(in_5));
endmodule
