// Logisim project Led 01.circ as structural Verilog: 3 circuits, main circuit main
module main (
  input  C,
  input  D,
  input  E,
  input  F,
  input  G,
  output out_6
);

  wire and_1_out, and_2_out, and_3_out, and_4_out, and_5_out, and_6_out, and_7_out, not_1_out, not_2_out,
       not_3_out, not_4_out, not_5_out, not_6_out, not_7_out;

  not not_1 (not_1_out, D);
  not not_2 (not_2_out, E);
  not not_3 (not_3_out, F);
  not not_4 (not_4_out, G);
  not not_5 (not_5_out, C);
  not not_6 (not_6_out, C);
  not not_7 (not_7_out, F);
  and and_1 (and_1_out, D, C);
  and and_2 (and_2_out, not_5_out, not_3_out, not_4_out);
  and and_3 (and_3_out, not_5_out, E);
  and and_4 (and_4_out, not_1_out, not_2_out, not_3_out);
  and and_5 (and_5_out, not_1_out, F, not_4_out);
  and and_6 (and_6_out, not_6_out, F, G);
  and and_7 (and_7_out, not_1_out, E, not_7_out, G);
  or or_1 (out_6, and_1_out, and_2_out, and_3_out, and_4_out, and_5_out, and_6_out, and_7_out);
endmodule

module L01 (
  input  c,
  input  d,
  input  e,
  input  f,
  input  g,
  output s
);

  wire and_1_out, and_2_out, and_3_out, and_4_out, and_5_out, and_6_out, and_7_out, not_1_out, not_2_out,
       not_3_out, not_4_out, not_5_out, not_6_out, not_7_out, not_8_out, not_9_out, not_10_out, not_11_out,
       not_12_out;

  not not_1 (not_1_out, c);
  not not_2 (not_2_out, d);
  not not_3 (not_3_out, c);
  not not_4 (not_4_out, f);
  not not_5 (not_5_out, g);
  not not_6 (not_6_out, d);
  not not_7 (not_7_out, f);
  not not_8 (not_8_out, c);
  not not_9 (not_9_out, c);
  not not_10 (not_10_out, e);
  not not_11 (not_11_out, f);
  not not_12 (not_12_out, g);
  and and_1 (and_1_out, not_1_out, not_2_out);
  and and_2 (and_2_out, not_3_out, not_4_out, not_5_out);
  and and_3 (and_3_out, not_6_out, not_7_out, g);
  and and_4 (and_4_out, not_8_out, f, g);
  and and_5 (and_5_out, not_9_out, e);
  and and_6 (and_6_out, c, not_10_out, not_11_out);
  and and_7 (and_7_out, c, f, not_12_out);
  or or_1 (s, and_1_out, and_2_out, and_3_out, and_4_out, and_5_out, and_6_out, and_7_out);
endmodule

module L02 (
  input  c,
  input  d,
  input  e,
  input  f,
  input  g,
  output s
);

  wire and_1_out, and_2_out, and_3_out, and_4_out, and_5_out, and_6_out, not_1_out, not_2_out, not_3_out,
       not_4_out, not_5_out, not_6_out, not_7_out, not_8_out, not_9_out, not_10_out, not_11_out, not_12_out;

  not not_1 (not_1_out, d);
  not not_2 (not_2_out, f);
  not not_3 (not_3_out, g);
  not not_4 (not_4_out, d);
  not not_5 (not_5_out, c);
  not not_6 (not_6_out, d);
  not not_7 (not_7_out, g);
  not not_8 (not_8_out, f);
  not not_9 (not_9_out, c);
  not not_10 (not_10_out, g);
  not not_11 (not_11_out, e);
  not not_12 (not_12_out, f);
  and and_1 (and_1_out, not_1_out, not_2_out, not_3_out);
  and and_2 (and_2_out, not_4_out, f, g);
  and and_3 (and_3_out, not_5_out, not_6_out, e, not_7_out);
  and and_4 (and_4_out, d, not_8_out, g);
  and and_5 (and_5_out, not_9_out, d, f, not_10_out);
  and and_6 (and_6_out, c, not_11_out, not_12_out);
  or or_1 (s, and_1_out, and_2_out, and_3_out, and_4_out, and_5_out, and_6_out);
endmodule
