// Logisim project trab.circ as structural Verilog: 1 circuit, main circuit main
module main (
  input  [7:0] in_1,
  input  [7:0] in_2,
  input  [7:0] in_3,
  input  [7:0] in_4,
  input  [1:0] in_5,
  input  [7:0] X,
  input  [1:0] m,
  input  in_8,
  input  in_9,
  input  in_10,
  input  in_11,
  input  in_12,
  input  in_13,
  input  in_14,
  input  in_15,
  output [7:0] out_16,
  output [7:0] out_17,
  output [7:0] out_18,
  output [7:0] out_19,
  output [7:0] out_20,
  output [1:0] n,
  output [2:0] out_22
);

  Multiplexer #(.select(2), .width(8)) multiplexer_1 (
    .in0(in_1), .in1(in_2), .in2(in_3), .in3(in_4), .out(out_18), .sel(in_5));  // open: en
  Priority_Encoder priority_encoder_1 (
    .in0(in_8), .in1(in_9), .in2(in_10), .in3(in_11), .in4(in_12), .in5(in_13), .in6(in_14), .in7(in_15),
    .out(out_22));  // open: en_in, gs, en_out
  Demultiplexer #(.select(2), .width(8)) demultiplexer_1 (
    .out0(out_16), .out1(out_17), .out2(out_19), .out3(out_20), .in(out_18), .sel(in_5));  // open: en
  BitSelector #(.group(2)) bitselector_1 (.in(X), .out(n), .sel(m));

  // Notes on the sheet:
  //   Mostra na saída qual o bit mais significativo da entrada
  //   Divide a entrada de tamanho X bits, em grupos de n bits.
  //   Cada grupo de bits pode ser selecionado utilizando um select de m bits.
endmodule
