// Logisim project decade-counter.circ as structural Verilog: 1 circuit, main circuit main
module main (
  input  J,
  input  in_2,
  output _1,
  output _2,
  output _4,
  output _8
);

  wire and_1_out, j_k_ff_1_qn, j_k_ff_2_qn, j_k_ff_3_qn;

  J_K_Flip_Flop j_k_ff_1 (.J(J), .clk(in_2), .K(J), .Q(_1), .Qn(j_k_ff_1_qn), .reset(and_1_out));  // open: preset, en
  J_K_Flip_Flop j_k_ff_2 (
    .J(J), .clk(j_k_ff_1_qn), .K(J), .Q(_2), .Qn(j_k_ff_2_qn), .reset(and_1_out));  // open: preset, en
  J_K_Flip_Flop j_k_ff_3 (
    .J(J), .clk(j_k_ff_2_qn), .K(J), .Q(_4), .Qn(j_k_ff_3_qn), .reset(and_1_out));  // open: preset, en
  J_K_Flip_Flop j_k_ff_4 (.J(J), .clk(j_k_ff_3_qn), .K(J), .Q(_8), .reset(and_1_out));  // open: Qn, preset, en
  and and_1 (and_1_out, _8, j_k_ff_3_qn, _2, j_k_ff_1_qn);
endmodule
